// Logisim project lab_2.circ as structural Verilog: 12 circuits, main circuit coder
module coder (
  input  _0,
  input  _1,
  input  _2,
  input  _3,
  input  _4,
  input  _5,
  input  _6,
  input  _7,
  input  _8,
  input  _9,
  output q1,
  output q2,
  output q4,
  output q8
);

  or or_1 (q1, _1, _3, _7, _9, _5);
  or or_2 (q2, _2, _3, _6, _7);
  or or_3 (q4, _4, _5, _6, _7);
  or or_4 (q8, _8, _9);
endmodule

module sum (
  input  in_1,
  input  in_2,
  input  in_3,
  output out_4,
  output out_5
);

  wire and_1_out, and_2_out, xor_1_out;

  xor xor_1 (xor_1_out, in_2, in_3);
  and and_1 (and_1_out, in_2, in_3);
  xor xor_2 (out_5, in_1, xor_1_out);
  and and_2 (and_2_out, in_1, xor_1_out);
  or or_1 (out_4, and_2_out, and_1_out);
endmodule

module decoder (
  input  D1,
  input  D2,
  input  D4,
  input  D8,
  output _0,
  output _1,
  output _2,
  output _3,
  output _4,
  output _5,
  output _6,
  output _7,
  output _8,
  output _9,
  output _10,
  output _11,
  output _12,
  output _13,
  output _14,
  output _15
);

  wire not_1_out, not_2_out, not_3_out, not_4_out;

  // Probe on D1
  not not_1 (not_1_out, D1);
  not not_2 (not_2_out, D2);
  not not_3 (not_3_out, D4);
  not not_4 (not_4_out, D8);
  // Probe on not_1_out
  // Probe on D2
  // Probe on D4
  // Probe on not_2_out
  // Probe on not_3_out
  // Probe on D8
  // Probe on not_4_out
  and and_1 (_0, not_1_out, not_2_out, not_3_out, not_4_out);
  and and_2 (_1, D1, not_2_out, not_3_out, not_4_out);
  and and_3 (_2, not_1_out, D2, not_3_out, not_4_out);
  and and_4 (_3, D1, D2, not_3_out, not_4_out);
  and and_5 (_4, not_1_out, not_2_out, D4, not_4_out);
  and and_6 (_5, D1, not_2_out, D4, not_4_out);
  and and_7 (_6, not_1_out, D2, D4, not_4_out);
  and and_8 (_7, D1, D2, D4, not_4_out);
  and and_9 (_8, not_1_out, not_2_out, not_3_out, D8);
  and and_10 (_9, D1, not_2_out, not_3_out, D8);
  and and_11 (_10, not_1_out, D2, not_3_out, D8);
  and and_12 (_11, D1, D2, not_3_out, D8);
  and and_13 (_12, not_1_out, not_2_out, D4, D8);
  and and_14 (_13, D1, not_2_out, D4, D8);
  and and_15 (_14, not_1_out, D2, D4, D8);
  and and_16 (_15, D8, D4, D2, D1);

  // Notes on the sheet:
  //   D1~D1
  //   D2~D2
  //   D4~D4
  //   D8~D8
endmodule

module _4_sum (
  input  in_1,
  input  in_2,
  input  in_3,
  input  in_4,
  input  in_5,
  input  in_6,
  input  in_7,
  input  in_8,
  input  in_9,
  output out_10,
  output out_11,
  output out_12,
  output out_13,
  output out_14
);

  wire sum_2_out_4, sum_3_out_4, sum_4_out_4;

  sum sum_1 (.in_1(sum_2_out_4), .in_2(in_1), .in_3(in_5), .out_5(out_10), .out_4(out_14));
  sum sum_2 (.in_1(sum_3_out_4), .in_2(in_2), .in_3(in_6), .out_5(out_11), .out_4(sum_2_out_4));
  sum sum_3 (.in_1(sum_4_out_4), .in_2(in_3), .in_3(in_7), .out_5(out_12), .out_4(sum_3_out_4));
  sum sum_4 (.in_1(in_9), .in_2(in_4), .in_3(in_8), .out_5(out_13), .out_4(sum_4_out_4));
endmodule

module main (
  input  _0,
  input  _1,
  input  _2,
  input  _3,
  input  _4,
  input  _5,
  input  _6,
  input  _7,
  input  _8,
  input  _9,
  input  _0_2,
  input  _1_2,
  input  _2_2,
  input  _3_2,
  input  _4_2,
  input  _5_2,
  input  _6_2,
  input  _7_2,
  input  _8_2,
  input  _9_2,
  input  in_21,
  output out_22,
  output out_23
);

  wire and_2_out, and_3_out, coder_1_q1, coder_1_q2, coder_1_q4, coder_1_q8, coder_2_q1, coder_2_q2,
       coder_2_q4, coder_2_q8, n4_sum_1_out_10, n4_sum_1_out_11, n4_sum_1_out_12, n4_sum_1_out_13, not_1_out,
       xor_1_out, xor_2_out, xor_3_out, xor_4_out;
  wire [3:0] buffer_1_out, not_2_out;

  coder coder_1 (
    ._0(_0), ._1(_1), ._2(_2), ._3(_3), ._4(_4), ._5(_5), ._6(_6), ._7(_7), ._8(_8), ._9(_9),
    .q1(coder_1_q1), .q2(coder_1_q2), .q4(coder_1_q4), .q8(coder_1_q8));
  coder coder_2 (
    ._0(_0_2), ._1(_1_2), ._2(_2_2), ._3(_3_2), ._4(_4_2), ._5(_5_2), ._6(_6_2), ._7(_7_2), ._8(_8_2),
    ._9(_9_2), .q1(coder_2_q1), .q2(coder_2_q2), .q4(coder_2_q4), .q8(coder_2_q8));
  xor xor_1 (xor_1_out, coder_2_q8, in_21);
  xor xor_2 (xor_2_out, coder_2_q4, in_21);
  xor xor_3 (xor_3_out, coder_2_q2, in_21);
  xor xor_4 (xor_4_out, coder_2_q1, in_21);
  and and_1 (out_22, out_23, and_3_out, in_21);
  _4_sum u_4_sum_1 (
    .in_1(coder_1_q8), .in_2(coder_1_q4), .in_3(coder_1_q2), .in_4(coder_1_q1), .in_5(xor_1_out),
    .in_6(xor_2_out), .in_7(xor_3_out), .in_8(xor_4_out), .in_9(out_22), .out_10(n4_sum_1_out_10),
    .out_11(n4_sum_1_out_11), .out_12(n4_sum_1_out_12), .out_13(n4_sum_1_out_13), .out_14(out_23));
  not not_1 (not_1_out, and_2_out);
  Hex_Digit_Display hex_digit_display_1 (.value(buffer_1_out));  // open: dp
  buf buffer_1 (buffer_1_out[0], n4_sum_1_out_13);
  buf buffer_2 (buffer_1_out[1], n4_sum_1_out_12);
  buf buffer_3 (buffer_1_out[2], n4_sum_1_out_11);
  buf buffer_4 (buffer_1_out[3], n4_sum_1_out_10);
  and and_2 (and_2_out, ~out_23, in_21);  // AND_Gate
  and and_3 (and_3_out, out_23, in_21);
  Hex_Digit_Display hex_digit_display_2 ();  // open: value, dp
  not not_2 (not_2_out[0], n4_sum_1_out_13);
  not not_3 (not_2_out[1], n4_sum_1_out_12);
  not not_4 (not_2_out[2], n4_sum_1_out_11);
  not not_5 (not_2_out[3], n4_sum_1_out_10);
  Hex_Digit_Display hex_digit_display_3 (.value(not_2_out));  // open: dp
endmodule

module com (
  input  in_1,
  input  in_2,
  output out_3,
  output out_4
);

  xnor xnor_1 (out_3, in_1, in_2);
  and and_1 (out_4, in_1, ~in_2);  // AND_Gate
endmodule

module com_4bit (
  input  in_1,
  input  in_2,
  input  in_3,
  input  in_4,
  input  in_5,
  input  in_6,
  input  in_7,
  input  in_8,
  output A_B,
  output A_B_2,
  output A_B_3
);

  wire and_2_out, and_3_out, and_4_out, com_1_out_3, com_1_out_4, com_2_out_3, com_2_out_4, com_3_out_3,
       com_3_out_4, com_4_out_3, com_4_out_4;

  com com_1 (.in_1(in_1), .in_2(in_5), .out_3(com_1_out_3), .out_4(com_1_out_4));
  com com_2 (.in_1(in_2), .in_2(in_6), .out_3(com_2_out_3), .out_4(com_2_out_4));
  com com_3 (.in_1(in_3), .in_2(in_7), .out_3(com_3_out_3), .out_4(com_3_out_4));
  com com_4 (.in_1(in_4), .in_2(in_8), .out_3(com_4_out_3), .out_4(com_4_out_4));
  and and_1 (A_B, com_1_out_3, com_2_out_3, com_3_out_3, com_4_out_3);
  and and_2 (and_2_out, com_1_out_4, com_2_out_3, com_3_out_3, com_4_out_3);
  and and_3 (and_3_out, com_3_out_3, com_4_out_3, com_2_out_4);
  and and_4 (and_4_out, com_3_out_4, com_4_out_3);
  or or_1 (A_B_3, and_2_out, and_3_out, and_4_out, com_4_out_4);
  nor nor_1 (A_B_2, A_B, A_B_3);
endmodule

module com_4bit_and_coder (
  input  _0,
  input  _1,
  input  _2,
  input  _3,
  input  _4,
  input  _5,
  input  _6,
  input  _7,
  input  _8,
  input  _9,
  input  _0_2,
  input  _1_2,
  input  _2_2,
  input  _3_2,
  input  _4_2,
  input  _5_2,
  input  _6_2,
  input  _7_2,
  input  _8_2,
  input  _9_2
);

  wire coder_1_q1, coder_1_q2, coder_1_q4, coder_1_q8, coder_2_q1, coder_2_q2, coder_2_q4, coder_2_q8,
       com_4bit_1_a_b, com_4bit_1_a_b_2, com_4bit_1_a_b_3;

  coder coder_1 (
    ._0(_0), ._1(_1), ._2(_2), ._3(_3), ._4(_4), ._5(_5), ._6(_6), ._7(_7), ._8(_8), ._9(_9),
    .q1(coder_1_q1), .q2(coder_1_q2), .q4(coder_1_q4), .q8(coder_1_q8));
  coder coder_2 (
    ._0(_0_2), ._1(_1_2), ._2(_2_2), ._3(_3_2), ._4(_4_2), ._5(_5_2), ._6(_6_2), ._7(_7_2), ._8(_8_2),
    ._9(_9_2), .q1(coder_2_q1), .q2(coder_2_q2), .q4(coder_2_q4), .q8(coder_2_q8));
  com_4bit com_4bit_1 (
    .in_1(coder_1_q1), .in_2(coder_1_q2), .in_3(coder_1_q4), .in_4(coder_1_q8), .in_5(coder_2_q1),
    .in_6(coder_2_q2), .in_7(coder_2_q4), .in_8(coder_2_q8), .A_B(com_4bit_1_a_b), .A_B_2(com_4bit_1_a_b_2),
    .A_B_3(com_4bit_1_a_b_3));
  LED led_1 (.in(com_4bit_1_a_b));
  LED led_2 (.in(com_4bit_1_a_b_2));
  LED led_3 (.in(com_4bit_1_a_b_3));
endmodule

module miltiply (
  input  A8,
  input  A4,
  input  A2,
  input  A1,
  input  B1,
  input  B2,
  input  B4,
  input  B8,
  output q128,
  output q64,
  output q32,
  output q16,
  output q8,
  output q4,
  output q2,
  output q1
);

  wire and_1_out, and_5_out, and_6_out, and_7_out, and_8_out, and_9_out, and_10_out, and_12_out, and_13_out,
       and_14_out, and_15_out, and_16_out, n4_sum_1_out_10, n4_sum_1_out_11, n4_sum_1_out_12,
       n4_sum_1_out_14, n4_sum_2_out_10, n4_sum_2_out_11, n4_sum_2_out_12, n4_sum_2_out_14;

  and and_1 (and_1_out, A8, B1);
  and and_2 (and_1_out, A4, B1);
  and and_3 (and_1_out, A2, B1);
  and and_4 (q1, B1, A1);
  and and_5 (and_5_out, A8, B2);
  and and_6 (and_6_out, A4, B2);
  and and_7 (and_7_out, A2, B2);
  and and_8 (and_8_out, B2, A1);
  _4_sum u_4_sum_1 (
    .in_1(and_5_out), .in_2(and_6_out), .in_3(and_7_out), .in_4(and_8_out), .in_5(and_1_out),
    .in_6(and_1_out), .in_7(and_1_out), .in_8(and_1_out), .in_9(and_1_out), .out_10(n4_sum_1_out_10),
    .out_11(n4_sum_1_out_11), .out_12(n4_sum_1_out_12), .out_13(q2), .out_14(n4_sum_1_out_14));
  and and_9 (and_9_out, A8, B4);
  and and_10 (and_10_out, A4, B4);
  and and_11 (and_9_out, A2, B4);
  and and_12 (and_12_out, B4, A1);
  _4_sum u_4_sum_2 (
    .in_1(and_9_out), .in_2(and_10_out), .in_3(and_9_out), .in_4(and_12_out), .in_5(n4_sum_1_out_14),
    .in_6(n4_sum_1_out_10), .in_7(n4_sum_1_out_11), .in_8(n4_sum_1_out_12), .in_9(and_1_out),
    .out_10(n4_sum_2_out_10), .out_11(n4_sum_2_out_11), .out_12(n4_sum_2_out_12), .out_13(q4),
    .out_14(n4_sum_2_out_14));
  and and_13 (and_13_out, A8, B8);
  and and_14 (and_14_out, A4, B8);
  and and_15 (and_15_out, A2, B8);
  and and_16 (and_16_out, B8, A1);
  _4_sum u_4_sum_3 (
    .in_1(and_13_out), .in_2(and_14_out), .in_3(and_15_out), .in_4(and_16_out), .in_5(n4_sum_2_out_14),
    .in_6(n4_sum_2_out_10), .in_7(n4_sum_2_out_11), .in_8(n4_sum_2_out_12), .in_9(and_1_out), .out_10(q64),
    .out_11(q32), .out_12(q16), .out_13(q8), .out_14(q128));
  // also tied to GND on the sheet: and_1_out
endmodule

module multiply_with_coder_and_decoder (
  input  _0,
  input  _1,
  input  _2,
  input  _3,
  input  _4,
  input  _5,
  input  _6,
  input  _7,
  input  _8,
  input  _9,
  input  _0_2,
  input  _1_2,
  input  _2_2,
  input  _3_2,
  input  _4_2,
  input  _5_2,
  input  _6_2,
  input  _7_2,
  input  _8_2,
  input  _9_2
);

  wire coder_1_q1, coder_1_q2, coder_1_q4, coder_1_q8, coder_2_q1, coder_2_q2, coder_2_q4, coder_2_q8,
       controlled_buffer_1_out, controlled_buffer_2_out, controlled_buffer_3_out, controlled_buffer_4_out,
       controlled_buffer_5_out, controlled_buffer_6_out, controlled_buffer_7_out, controlled_buffer_8_out,
       decoder_1__0, decoder_1__1, decoder_1__2, decoder_1__3, decoder_1__4, decoder_1__5, decoder_1__6,
       decoder_1__7, decoder_1__8, decoder_1__9, decoder_1__10, decoder_1__11, decoder_1__12, decoder_1__13,
       decoder_1__14, decoder_1__15, decoder_2__0, decoder_2__1, decoder_2__2, decoder_2__3, decoder_2__4,
       decoder_2__5, decoder_2__6, decoder_2__7, decoder_2__8, decoder_2__9, decoder_2__10, decoder_2__11,
       decoder_2__12, decoder_2__13, decoder_2__14, decoder_2__15, miltiply_1_q1, miltiply_1_q2,
       miltiply_1_q4, miltiply_1_q8, miltiply_1_q16, not_1_out;

  coder coder_1 (
    ._0(_0), ._1(_1), ._2(_2), ._3(_3), ._4(_4), ._5(_5), ._6(_6), ._7(_7), ._8(_8), ._9(_9),
    .q1(coder_1_q1), .q2(coder_1_q2), .q4(coder_1_q4), .q8(coder_1_q8));
  coder coder_2 (
    ._0(_0_2), ._1(_1_2), ._2(_2_2), ._3(_3_2), ._4(_4_2), ._5(_5_2), ._6(_6_2), ._7(_7_2), ._8(_8_2),
    ._9(_9_2), .q1(coder_2_q1), .q2(coder_2_q2), .q4(coder_2_q4), .q8(coder_2_q8));
  miltiply miltiply_1 (
    .A8(coder_1_q8), .A4(coder_1_q4), .A2(coder_1_q2), .A1(coder_1_q1), .B1(coder_2_q1), .B2(coder_2_q2),
    .B4(coder_2_q4), .B8(coder_2_q8), .q16(miltiply_1_q16), .q8(miltiply_1_q8), .q4(miltiply_1_q4),
    .q2(miltiply_1_q2), .q1(miltiply_1_q1));  // open: q128, q64, q32
  not not_1 (not_1_out, miltiply_1_q16);
  assign controlled_buffer_1_out = not_1_out ? miltiply_1_q1 : 1'bz;  // Controlled_Buffer controlled_buffer_1
  assign controlled_buffer_2_out = not_1_out ? miltiply_1_q2 : 1'bz;  // Controlled_Buffer controlled_buffer_2
  assign controlled_buffer_3_out = not_1_out ? miltiply_1_q4 : 1'bz;  // Controlled_Buffer controlled_buffer_3
  assign controlled_buffer_4_out = not_1_out ? miltiply_1_q8 : 1'bz;  // Controlled_Buffer controlled_buffer_4
  assign controlled_buffer_5_out = miltiply_1_q16 ? miltiply_1_q1 : 1'bz;  // Controlled_Buffer controlled_buffer_5
  assign controlled_buffer_6_out = miltiply_1_q16 ? miltiply_1_q2 : 1'bz;  // Controlled_Buffer controlled_buffer_6
  assign controlled_buffer_7_out = miltiply_1_q16 ? miltiply_1_q4 : 1'bz;  // Controlled_Buffer controlled_buffer_7
  assign controlled_buffer_8_out = miltiply_1_q16 ? miltiply_1_q8 : 1'bz;  // Controlled_Buffer controlled_buffer_8
  LED led_1 (.in(decoder_1__0));
  decoder decoder_1 (
    .D1(controlled_buffer_1_out), .D2(controlled_buffer_2_out), .D4(controlled_buffer_3_out),
    .D8(controlled_buffer_4_out), ._0(decoder_1__0), ._1(decoder_1__1), ._2(decoder_1__2), ._3(decoder_1__3),
    ._4(decoder_1__4), ._5(decoder_1__5), ._6(decoder_1__6), ._7(decoder_1__7), ._8(decoder_1__8),
    ._9(decoder_1__9), ._10(decoder_1__10), ._11(decoder_1__11), ._12(decoder_1__12), ._13(decoder_1__13),
    ._14(decoder_1__14), ._15(decoder_1__15));
  LED led_2 (.in(decoder_1__1));
  LED led_3 (.in(decoder_1__2));
  LED led_4 (.in(decoder_1__3));
  LED led_5 (.in(decoder_1__4));
  LED led_6 (.in(decoder_1__5));
  LED led_7 (.in(decoder_1__6));
  LED led_8 (.in(decoder_1__7));
  LED led_9 (.in(decoder_1__8));
  LED led_10 (.in(decoder_1__9));
  LED led_11 (.in(decoder_1__10));
  LED led_12 (.in(decoder_1__11));
  LED led_13 (.in(decoder_1__12));
  LED led_14 (.in(decoder_1__13));
  LED led_15 (.in(decoder_1__14));
  LED led_16 (.in(decoder_1__15));
  decoder decoder_2 (
    .D1(controlled_buffer_5_out), .D2(controlled_buffer_6_out), .D4(controlled_buffer_7_out),
    .D8(controlled_buffer_8_out), ._0(decoder_2__0), ._1(decoder_2__1), ._2(decoder_2__2), ._3(decoder_2__3),
    ._4(decoder_2__4), ._5(decoder_2__5), ._6(decoder_2__6), ._7(decoder_2__7), ._8(decoder_2__8),
    ._9(decoder_2__9), ._10(decoder_2__10), ._11(decoder_2__11), ._12(decoder_2__12), ._13(decoder_2__13),
    ._14(decoder_2__14), ._15(decoder_2__15));
  LED led_17 (.in(decoder_2__0));
  LED led_18 (.in(decoder_2__1));
  LED led_19 (.in(decoder_2__2));
  LED led_20 (.in(decoder_2__3));
  LED led_21 (.in(decoder_2__4));
  LED led_22 (.in(decoder_2__5));
  LED led_23 (.in(decoder_2__6));
  LED led_24 (.in(decoder_2__7));
  LED led_25 (.in(decoder_2__8));
  LED led_26 (.in(decoder_2__9));
  LED led_27 (.in(decoder_2__10));
  LED led_28 (.in(decoder_2__11));
  LED led_29 (.in(decoder_2__12));
  LED led_30 (.in(decoder_2__13));
  LED led_31 (.in(decoder_2__14));
  LED led_32 (.in(decoder_2__15));

  // Notes on the sheet:
  //   2
  //   3
  //   4
  //   5
  //   6
  //   7
  //   8
  //   9
  //   10
  //   11
  //   12
  //   13
  //   14
  //   15
  //   0
  //   1
  //   16
  //   17
  //   18
  //   19
  //   20
  //   21
  //   22
  //   23
  //   24
  //   25
  //   26
  //   27
  //   28
  //   29
  //   30
  //   31
endmodule

module algorythm_multiply (
  input  _0,
  input  _1,
  input  _2,
  input  _3,
  input  _4,
  input  _5,
  input  _6,
  input  _7,
  input  _8,
  input  _9,
  input  _0_2,
  input  _1_2,
  input  _2_2,
  input  _3_2,
  input  _4_2,
  input  _5_2,
  input  _6_2,
  input  _7_2,
  input  _8_2,
  input  in_20,
  input  _9_2
);

  wire and_1_out, and_2_out, and_3_out, and_4_out, and_5_out, and_6_out, and_7_out, and_8_out, CL_out,
       coder_1_q1, coder_1_q2, coder_1_q4, coder_1_q8, coder_2_q1, coder_2_q2, coder_2_q4, coder_2_q8,
       not_1_out, not_2_out, or_1_out, R_out, shift_register_1_q1, shift_register_1_q3, shift_register_1_q4,
       shift_register_1_q5, shift_register_2_q0, shift_register_2_q1, shift_register_2_q2;
  wire [7:0] sum_4bit_1_out_18;
  wire [7:1] register_1_q;

  Button CL (.out(CL_out));
  Button R (.out(R_out));
  coder coder_1 (
    ._0(_0), ._1(_1), ._2(_2), ._3(_3), ._4(_4), ._5(_5), ._6(_6), ._7(_7), ._8(_8), ._9(_9),
    .q1(coder_1_q1), .q2(coder_1_q2), .q4(coder_1_q4), .q8(coder_1_q8));
  coder coder_2 (
    ._0(_0_2), ._1(_1_2), ._2(_2_2), ._3(_3_2), ._4(_4_2), ._5(_5_2), ._6(_6_2), ._7(_7_2), ._8(_8_2),
    ._9(_9_2), .q1(coder_2_q1), .q2(coder_2_q2), .q4(coder_2_q4), .q8(coder_2_q8));
  or or_1 (or_1_out, shift_register_2_q0, shift_register_2_q1, shift_register_2_q2, shift_register_1_q1, shift_register_1_q1);
  LED led_1 (.in(or_1_out));
  not not_1 (not_1_out, in_20);
  Shift_Register shift_register_1 (
    .shift(not_1_out), .in(coder_2_q8), .clk(CL_out), .load(in_20), .d0(coder_2_q1), .d1(coder_2_q2),
    .q1(shift_register_1_q1), .d2(coder_2_q4), .q2(R_out), .d3(coder_2_q8), .q3(shift_register_1_q3),
    .d4(coder_2_q8), .q4(shift_register_1_q4), .d5(coder_2_q8), .q5(shift_register_1_q5), .d6(coder_2_q8),
    .q6(shift_register_1_q1), .d7(coder_2_q8), .q7(shift_register_1_q5));  // open: out, clr, q0
  Shift_Register #(.length(4)) shift_register_2 (
    .shift(not_1_out), .in(coder_2_q8), .clk(CL_out), .load(in_20), .clr(R_out), .d0(coder_1_q8),
    .q0(shift_register_2_q0), .d1(coder_1_q4), .q1(shift_register_2_q1), .d2(coder_1_q2),
    .q2(shift_register_2_q2), .d3(coder_1_q1), .q3(shift_register_1_q1));  // open: out
  and and_1 (and_1_out, shift_register_1_q1, shift_register_1_q5);
  and and_2 (and_2_out, shift_register_1_q1, shift_register_1_q1);
  and and_3 (and_3_out, shift_register_1_q1, shift_register_1_q5);
  and and_4 (and_4_out, shift_register_1_q1, shift_register_1_q4);
  and and_5 (and_5_out, shift_register_1_q1, shift_register_1_q3);
  and and_6 (and_6_out, shift_register_1_q1, shift_register_1_q5);
  and and_7 (and_7_out, shift_register_1_q1, shift_register_1_q1);
  and and_8 (and_8_out, shift_register_1_q1, shift_register_1_q3);
  sum_4bit sum_4bit_1 (
    .a7(and_1_out), .in_2(and_2_out), .in_3(and_3_out), .in_4(and_4_out), .in_5(and_5_out), .in_6(and_6_out),
    .a0(and_7_out), .in_8(and_8_out), .b7(register_1_q[1]), .in_10(register_1_q[1]), .in_11(register_1_q[2]),
    .in_12(register_1_q[3]), .in_13(register_1_q[4]), .in_14(coder_2_q8), .in_15(register_1_q[5]),
    .b0(register_1_q[6]), .in_17(register_1_q[7]), .out_18(sum_4bit_1_out_18[0]),
    .out_20(sum_4bit_1_out_18[1]), .out_21(sum_4bit_1_out_18[2]), .out_22(sum_4bit_1_out_18[3]),
    .out_23(sum_4bit_1_out_18[4]), .out_24(sum_4bit_1_out_18[5]), .out_25(sum_4bit_1_out_18[6]),
    .out_26(sum_4bit_1_out_18[7]));  // open: out_19
  not not_2 (not_2_out, in_20);
  // Probe on {register_1_q, register_1_q[1]}
  Register register_1 (
    .D(sum_4bit_1_out_18), .en(not_2_out), .Q({register_1_q, register_1_q[1]}), .clk(CL_out), .clr(R_out));
  // also tied to GND on the sheet: coder_2_q8

  // Notes on the sheet:
  //   FINAL
endmodule

module sum_4bit (
  input  a7,
  input  in_2,
  input  in_3,
  input  in_4,
  input  in_5,
  input  in_6,
  input  a0,
  input  in_8,
  input  b7,
  input  in_10,
  input  in_11,
  input  in_12,
  input  in_13,
  input  in_14,
  input  in_15,
  input  b0,
  input  in_17,
  output out_18,
  output out_19,
  output out_20,
  output out_21,
  output out_22,
  output out_23,
  output out_24,
  output out_25,
  output out_26
);

  wire sum_2_out_4, sum_3_out_4, sum_4_out_4, sum_5_out_4, sum_6_out_4, sum_7_out_4, sum_8_out_4;

  sum sum_1 (.in_1(sum_2_out_4), .in_2(a7), .in_3(b7), .out_5(out_18), .out_4(out_19));
  sum sum_2 (.in_1(sum_3_out_4), .in_2(in_2), .in_3(in_10), .out_5(out_20), .out_4(sum_2_out_4));
  sum sum_3 (.in_1(sum_4_out_4), .in_2(in_3), .in_3(in_11), .out_5(out_21), .out_4(sum_3_out_4));
  sum sum_4 (.in_1(sum_5_out_4), .in_2(in_4), .in_3(in_12), .out_5(out_22), .out_4(sum_4_out_4));
  sum sum_5 (.in_1(sum_6_out_4), .in_2(in_5), .in_3(in_13), .out_5(out_23), .out_4(sum_5_out_4));
  sum sum_6 (.in_1(sum_7_out_4), .in_2(in_6), .in_3(in_15), .out_5(out_24), .out_4(sum_6_out_4));
  sum sum_7 (.in_1(sum_8_out_4), .in_2(a0), .in_3(b0), .out_5(out_25), .out_4(sum_7_out_4));
  sum sum_8 (.in_1(in_14), .in_2(in_8), .in_3(in_17), .out_5(out_26), .out_4(sum_8_out_4));
endmodule
