// Logisim project scheme_task_3.circ as structural Verilog: 1 circuit, main circuit main
module main (
  input  y,
  input  x,
  input  z,
  output f1,
  output f2
);

  wire and_1_out, and_2_out, not_1_out, not_2_out, not_3_out, or_1_out, or_2_out;

  not not_1 (not_1_out, y);
  not not_2 (not_2_out, x);
  not not_3 (not_3_out, y);
  and and_1 (and_1_out, not_1_out, x);
  and and_2 (and_2_out, y, z);
  or or_1 (or_1_out, not_3_out, z);
  or or_2 (or_2_out, x, y);
  or or_3 (f1, and_1_out, not_2_out, and_2_out);
  xor xor_1 (f2, or_1_out, or_2_out);
endmodule
